# Fritzing sketch z_cam_io_focus (saved by Fritzing 0.9.3b)
breadboards: 2

parts:
  U1 = SLIDER [package=slider]
  B0 = Momentary Switch [package=ksa_sealed_tac_switch]
  B1 = Momentary Switch [package=ksa_sealed_tac_switch]
  B2 = Momentary Switch [package=ksa_sealed_tac_switch]
  B3 = Momentary Switch [package=ksa_sealed_tac_switch]
  B7 = Momentary Switch [package=ksa_sealed_tac_switch]
  R1 = Resistor [tolerance=±5% resistance=4.7k package=THT]
  Q1_BC547B = NPN-Transistor [package="TO92 [THT]"]
  Flash_TRG = Header 1 [package=smtra-256-8-6]
  Flash_GND = Header 1 [package=smtra-256-8-6]
  CAM_I/O_odd_pins = Header 6 [package=molex-1x6_lock]
  CAM_I/O_even_pins = Header 6 [package=molex-1x6_lock]
  Teensy1 = Teensy 2.0
  R2 = Resistor [tolerance=±5% resistance=4.7k package=THT]
  R3 = Resistor [tolerance=±5% resistance=4.7k package=THT]

nets:
  GND: U1.E, B0.1, B1.1, B2.1, B3.1, B7.2, Q1_BC547B.E, Flash_GND.1, CAM_I/O_odd_pins.11_GND, Teensy1.GND
  N1: U1.S, Teensy1.F0
  5V: U1.A, CAM_I/O_odd_pins.1_VCOM, CAM_I/O_even_pins.2_VCOM, Teensy1.VCC, R2.Pin_1, R3.Pin_1
  N2: B0.3, Teensy1.B0
  N3: B1.3, Teensy1.B1
  N4: B2.3, Teensy1.B2
  N5: B3.3, Teensy1.B3
  N6: B7.4, Teensy1.B7
  N7: R1.Pin_0, Teensy1.B4
  N8: R1.Pin_1, Q1_BC547B.B
  N9: Q1_BC547B.C, Flash_TRG.1
  N10: CAM_I/O_odd_pins.5_Rx, Teensy1.D3
  N11: CAM_I/O_odd_pins.SDA, Teensy1.D1, R3.Pin_0
  N12: CAM_I/O_even_pins.8_SCL, Teensy1.D0, R2.Pin_0
  N13: CAM_I/O_even_pins.6_Tx, Teensy1.D2

custom parts:
  Header 6: Header 6 Standard 6-pin 0.1 header. Use with straight break away headers (SKU : PRT-00116), right angle break away headers (PRT-00553), swiss pins (PRT-00743), machine pins (PRT-00117), and female headers (PRT-00115). Molex polarized connector foot print use with SKU : PRT-08094 with associated crimp pins and housings. NOTES ON THE VARIANTS LOCK and LOCK_LONGPADS... This footprint was designed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
  Header 6: Header 6 Standard 6-pin 0.1 header. Use with straight break away headers (SKU : PRT-00116), right angle break away headers (PRT-00553), swiss pins (PRT-00743), machine pins (PRT-00117), and female headers (PRT-00115). Molex polarized connector foot print use with SKU : PRT-08094 with associated crimp pins and housings. NOTES ON THE VARIANTS LOCK and LOCK_LONGPADS... This footprint was designed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
